# Fritzing sketch Wiring Diagram (saved by Fritzing 0.9.2b)
breadboards: 1

parts:
  Bauteil1 = Arduino Uno (Rev3)
  Q1 = Basic FET N-Channel [package="TO220 [THT]"]
  Q2 = Basic FET N-Channel [package="TO220 [THT]"]
  Q3 = Basic FET N-Channel [package="TO220 [THT]"]
  R1 = Resistor [tolerance=±5% resistance=220 package=THT]
  R2 = Resistor [tolerance=±5% resistance=220 package=THT]
  R3 = Resistor [tolerance=±5% resistance=220 package=THT]
  Power_plug1 = Power plug
  R4 = Resistor [tolerance=±5% resistance=10k package=THT]
  R5 = Resistor [tolerance=±5% resistance=4.7k package=THT]
  J2 = female pin header, 4 pins [form="♀ (female)"]
  J1 = female pin header, 4 pins [form="♀ (female)"]
  R6 = Resistor [tolerance=±5% resistance=10k package=THT]
  R7 = Resistor [tolerance=±5% resistance=10k package=THT]
  R8 = Resistor [tolerance=±5% resistance=10k package=THT]

nets:
  N1: Bauteil1.D9_PWM, R1.Pin_1
  N2: Bauteil1.D10_PWM/SS, R2.Pin_1
  N3: Bauteil1.D11_PWM/MOSI, R3.Pin_1
  N4: Bauteil1.D2, J1.pin2
  N5: Bauteil1.D3_PWM, R5.Pin_0
  N6: Bauteil1.5V, J1.pin4
  GND: Bauteil1.GND, Q1.source, Q2.source, Q3.source, Power_plug1.GND, R4.Pin_0, J1.pin3, R6.Pin_1, R7.Pin_1, R8.Pin_1
  VIN: Bauteil1.VIN, Power_plug1.VCC, J2.pin4
  N7: Q1.gate, R3.Pin_0, R6.Pin_0
  N8: Q1.drain, J2.pin1
  N9: Q2.gate, R2.Pin_0, R7.Pin_0
  N10: Q2.drain, J2.pin2
  N11: Q3.gate, R1.Pin_0, R8.Pin_0
  N12: Q3.drain, J2.pin3
  N13: R4.Pin_1, R5.Pin_1, J1.pin1

notes:
  Bluetooth Module
  RX - TX - GND - 5V
  LED Stripes
  R - G - B - V+
  Input
  LED Stipe Voltage
  white: V+
  black: GND
  TX - RX
  Softserial
